# Fritzing sketch sandbox (saved by Fritzing 0.9.3b)
breadboards: 1

parts:
  Teensy1 = Teensy 4.0
  LED1 = LEDs [package=led10mm]
  LED2 = LEDs [package=led10mm]
  LED3 = LEDs [package=led10mm]
  Power_plug1 = Power plug
  RE2 = KY-040 Rotary encoder [package=THT]
  BTFL5050Amp1 = BTF-LIGHTING RGB/RGBW 5050 LED Mini Amplifier
  drehdings1 = Drehdings
  LED4 = LEDs [package=led10mm]

nets:
  GND: Teensy1.pin_1, Teensy1.pin_17, Teensy1.pin_32, LED1.A, LED2.A, LED3.A, Power_plug1.GND, RE2.GND, BTFL5050Amp1.GND, drehdings1.GND, LED4.A
  N1: Teensy1.pin_3, RE2.SW
  N2: Teensy1.pin_6, RE2.DT
  N3: Teensy1.pin_7, RE2.CLK
  N4: Teensy1.pin_10, drehdings1.FG_(OUT)
  N5: Teensy1.pin_13, drehdings1.PWM_(IN)
  N6: Teensy1.pin_24, BTFL5050Amp1.IN4
  N7: Teensy1.pin_25, BTFL5050Amp1.IN3
  N8: Teensy1.pin_26, BTFL5050Amp1.IN2
  N9: Teensy1.pin_27, BTFL5050Amp1.IN1
  VCC: Teensy1.pin33, Power_plug1.VCC, RE2.Vcc, BTFL5050Amp1.Vcc, drehdings1.Vcc
  N10: LED1.C, BTFL5050Amp1.OUT2
  N11: LED2.C, BTFL5050Amp1.OUT1
  N12: LED3.C, BTFL5050Amp1.OUT3
  N13: BTFL5050Amp1.OUT4, LED4.C

custom parts:
  Teensy 4.0: The Teensy is a complete USB-based microcontoller development system, in a very small footprint, capable of implementing many types of projects. All programming is done via the USB port. No special programmer is needed, only a standard micro-USB cable and a PC or Macintosh with a USB port.
  KY-040 Rotary encoder: KY-040 Rotary Encoder with switch on breakout borad from AZ Delivery
  BTF-LIGHTING RGB/RGBW 5050 LED Mini Amplifier: Slim 12V5A or DC24V5A amplifier for BTF-LIGHTNING 5050SMD LED strips
  Drehdings: Brushless DC fan motor with PWM control and integrated hall sensor. Equipped with experimental rotation object.
